// Logisim project oblig2.circ as structural Verilog: 5 circuits, main circuit main
module main (
  input  Reset,
  input  [3:0] in_2,
  input  in_3,
  input  in_4,
  output [7:0] Instruction,
  output [7:0] Dataminne,
  output [3:0] out_7
);

  wire clock_1_out, decode_1_out_2, decode_1_out_3, decode_1_out_4, decode_1_out_5, or_1_out, or_2_out,
       or_3_out, Reset_out;
  wire [3:0] counter_1_out_3;
  wire [7:0] controlled_buffer_1_out, MSB_LSB_out_4, R_q;

  Clock clock_1 (.out(clock_1_out));
  Button u_Reset (.out(Reset_out));
  Counter counter_1 (.in_1(clock_1_out), .in_2(Reset_out), .out_3(counter_1_out_3));
  RAM_part #(.addrWidth(4), .bus("asynch")) ram_1 (
    .addr(counter_1_out_3), .data(Instruction), .clr(Reset));  // open: sel, ld
  Decode decode_1 (
    .in_1(Instruction[7:4]), .out_2(decode_1_out_2), .out_3(decode_1_out_3), .out_4(decode_1_out_4),
    .out_5(decode_1_out_5));
  LSB_MSB MSB_LSB (.in_1(R_q), .in_2(Instruction[3:0]), .LSB_0__MSB_1(decode_1_out_3), .out_4(MSB_LSB_out_4));
  // RAM ram_2: pin names not known; wires that end beside it: in_2, in_4, in_3, out_7
  assign controlled_buffer_1_out = or_1_out ? MSB_LSB_out_4 : 8'bz;  // Controlled_Buffer controlled_buffer_1
  or or_1 (or_1_out, decode_1_out_2, decode_1_out_3);
  or or_2 (or_2_out, decode_1_out_2, decode_1_out_3, decode_1_out_4);
  Register #(.trigger("falling")) R (
    .D(controlled_buffer_1_out), .en(or_2_out), .Q(R_q), .clk(clock_1_out), .clr(Reset_out));
  assign controlled_buffer_1_out = decode_1_out_5 ? R_q : 8'bz;  // Controlled_Buffer controlled_buffer_2
  or or_3 (or_3_out, decode_1_out_4, decode_1_out_5);
  RAM_part #(.addrWidth(4)) ram_3 (
    .addr(Instruction[3:0]), .data(controlled_buffer_1_out), .sel(or_3_out), .clk(clock_1_out),
    .ld(decode_1_out_4), .clr(Reset_out));
  assign Dataminne = or_3_out ? controlled_buffer_1_out : 8'bz;  // Controlled_Buffer controlled_buffer_3
endmodule

// Count
module Counter (
  input  in_1,
  input  in_2,
  output [3:0] out_3
);

  wire adder_1_cout, not_1_out;
  wire [3:0] adder_1_out;

  Register #(.width(4), .trigger("falling")) register_1 (
    .D(adder_1_out), .en(not_1_out), .Q(out_3), .clk(in_1), .clr(in_2));
  not not_1 (not_1_out, adder_1_cout);
  Adder #(.width(4)) adder_1 (.a(4'b0001), .b(out_3), .out(adder_1_out), .cout(adder_1_cout));  // open: cin
endmodule

module RAM (
  input  [3:0] Store,
  input  [3:0] Address,
  input  Store_2,
  input  Reset,
  output [3:0] Load
);

  wire not_1_out;

  assign Load = Store_2 ? Store : 4'bz;  // Controlled_Buffer controlled_buffer_1
  not not_1 (not_1_out, Store_2);
  RAM_part #(.addrWidth(4), .dataWidth(4), .bus("asynch")) ram_1 (
    .addr(Address), .data(Load), .ld(not_1_out), .clr(Reset));  // open: sel
endmodule

// Decoder
module Decode (
  input  [3:0] in_1,
  output out_2,
  output out_3,
  output out_4,
  output out_5
);

  Decoder #(.select(4), .enable("false")) decoder_1 (
    .out8(out_2), .out9(out_3), .out10(out_4), .out11(out_5), .sel(in_1));  // open: out0, out1, out2, out3, out4, out5, out6, out7, out12, out13, out14, out15
endmodule

module LSB_MSB (
  input  [7:0] in_1,
  input  [3:0] in_2,
  input  LSB_0__MSB_1,
  output [7:0] out_4
);

  wire not_1_out, not_2_out;

  not not_1 (not_1_out, LSB_0__MSB_1);
  assign out_4[3:0] = LSB_0__MSB_1 ? in_1[3:0] : 4'bz;  // Controlled_Buffer controlled_buffer_1
  assign out_4[7:4] = LSB_0__MSB_1 ? in_2 : 4'bz;  // Controlled_Buffer controlled_buffer_2
  not not_2 (not_2_out, LSB_0__MSB_1);
  assign out_4[7:4] = not_1_out ? in_1[7:4] : 4'bz;  // Controlled_Buffer controlled_buffer_3
  assign out_4[3:0] = not_2_out ? in_2 : 4'bz;  // Controlled_Buffer controlled_buffer_4
endmodule
